# Fritzing sketch tutorial_sketch_01 (saved by Fritzing 0.9.3b)
breadboards: 1

parts:
  VCC1 = Battery block 9V
  R1 = Resistor [tolerance=±5% resistance=1k package=THT]
  LED1 = smd LED [color="Red (633nm)" package="0603 [SMD]"]
  S1 = SWITCH-MOMENTARY-2 [package=tactile_switch_smd-2]

nets:
  N1: VCC1.-, LED1.cathode
  N2: VCC1.+, R1.Pin_0
  N3: R1.Pin_1, S1.1
  N4: LED1.anode, S1.2
