# Fritzing sketch tutorial_sketch_02 (saved by Fritzing 0.9.3b)
breadboards: 1

parts:
  VCC1 = Battery block 9V
  R1 = Resistor [tolerance=±5% resistance=100 package="0805 [SMD]"]
  R2 = Resistor [tolerance=±5% resistance=47k package="0805 [SMD]"]
  R3 = Resistor [tolerance=±5% resistance=47k package="0805 [SMD]"]
  LED1 = LED - 5mm [color="Red (633nm)" package="5 mm [THT]"]
  LED2 = LED - 5mm [color="Red (633nm)" package="5 mm [THT]"]
  Q1 = NPN-Transistor [part_number=BC547 package="TO92 [THT]"]
  Q2 = NPN-Transistor [part_number=BC547 package="TO92 [THT]"]
  R4 = Resistor [tolerance=±5% resistance=100 package=THT]
  C1 = Electrolytic Capacitor [capacitance=10µF package="100 mil [THT, electrolytic]"]
  C2 = Electrolytic Capacitor [capacitance=1µF package="100 mil [THT, electrolytic]"]

nets:
  N1: VCC1.-, R1.Pin_0, R2.Pin_0, R3.Pin_0, R4.Pin_0
  N2: VCC1.+, Q1.E, Q2.E
  N3: R1.Pin_1, LED1.anode
  N4: R2.Pin_1, Q2.B, C1.-
  N5: R3.Pin_1, Q1.B, C2.+
  N6: LED1.cathode, Q1.C, C1.+
  N7: LED2.cathode, Q2.C, C2.-
  N8: LED2.anode, R4.Pin_1
