# Fritzing sketch tutorial_sketch_03 (saved by Fritzing 0.9.3b)
breadboards: 1

parts:
  U1 = 555 Timer [package="DIP8 [THT]"]
  VCC1 = Battery block 9V
  R1 = Resistor [tolerance=±5% resistance=1k package=THT]
  R2 = Resistor [tolerance=±5% resistance=470k package=THT]
  R3 = Resistor [tolerance=±5% resistance=1k package=THT]
  C2 = Ceramic Capacitor [capacitance=0.01µF package="100 mil [THT, multilayer]"]
  C1 = Tantalum Capacitor [capacitance=1μF package="100 mil [THT, tantalum]"]
  LED1 = LED - 5mm [color="Red (633nm)" package="5 mm [THT]"]

nets:
  N1: U1.Ground, VCC1.-, C2.0, C1.-, LED1.cathode
  N2: U1.Trigger, U1.Threshold, R2.Pin_1, C1.+
  N3: U1.Output, R3.Pin_0
  N4: U1.Reset, U1.Vcc_Supply_Voltage, VCC1.+, R1.Pin_0
  N5: U1.Control_Voltage, C2.1
  N6: U1.Discharge, R1.Pin_1, R2.Pin_0
  N7: R3.Pin_1, LED1.anode
